# Fritzing sketch scheme (saved by Fritzing 0.9.3b)
breadboards: 1

parts:
  M1 = DOIT Esp32 DevKit v1 (30 pins long, 11 pins width) [part_number=ESP32S-PIN30]
  R1 = Resistor [tolerance=±5% resistance=220 package=THT]
  R2 = Resistor [tolerance=±5% resistance=220 package=THT]
  S1 = Pushbutton [package="[THT]"]
  R3 = Resistor [tolerance=±5% resistance=220 package=THT]
  LED1 = LED - 3mm [color="Red (633nm)" package="3 mm [THT]"]
  LED2 = smd LED [color="Blue (430nm)" package="0603 [SMD]"]

nets:
  N1: M1.GND, R1.Pin_1, R2.Pin_0, R3.Pin_1
  N2: M1.D14, LED1.cathode
  N3: M1.D12, S1.Pin_1, S1.Pin_2, R3.Pin_0
  N4: M1.D13, LED2.anode
  N5: M1.VIN, S1.Pin_3, S1.Pin_4
  N6: R1.Pin_0, LED1.anode
  N7: R2.Pin_1, LED2.cathode

custom parts:
  DOIT Esp32 DevKit v1 (30 pins long, 11 pins width): The DOIT Esp32 DevKit v1 is one of the development board created by DOIT to evaluate the ESP-WROOM-32 module. It is based on the ESP32 microcontroller that boasts Wifi, Bluetooth, Ethernet and Low Power support all in a single chip. (vanepp) made breadboard work, adjusted pin numbering and labels and reduced size of schematic and cleaned up pcb. This chip is 30pins long (2 x15) and 11 pins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
